// Logisim project CONTADOR_AULA4.circ as structural Verilog: 1 circuit, main circuit main
module main (
);

  wire C1, C2;
  wire [3:0] register_1_q, register_1_q_2;
  wire [7:0] adder_1_out;

  Adder adder_1 (.a({register_1_q_2, register_1_q}), .b(8'h1), .out(adder_1_out));  // open: cin, cout
  Button CLOCK (.out(C1));
  Button RESET (.out(C2));
  Hex_Digit_Display hex_digit_display_1 (.value(register_1_q_2));  // open: dp
  Register register_1 (.D(adder_1_out), .clk(C1), .Q({register_1_q_2, register_1_q}), .clr(C2));  // open: en
  Hex_Digit_Display hex_digit_display_2 (.value(register_1_q));  // open: dp
  // Digital_Oscilloscope digital_oscilloscope_1: pin names not known; wires that end beside it: C1, register_1_q[0], register_1_q[1], register_1_q[2], register_1_q[3], register_1_q_2[0], register_1_q_2[1], register_1_q_2[2], register_1_q_2[3], C2
endmodule
