// Logisim project cpu_1_unitau.circ as structural Verilog: 1 circuit, main circuit main
module main (
  input  [7:0] ENTRADA_DE_DADOS,
  output [7:0] SAIDA_DE_DADOS
);

  wire CLOCK_out, RESET_out;
  wire [7:0] adder_1_out, adder_2_out, BUF_E_D_out, REG_ACU_q, REG_D_q, REG_E_D_q, register_1_q, rom_1_data_2;
  wire [11:0] rom_1_data;

  Register REG_E_D (.D(ENTRADA_DE_DADOS), .clk(rom_1_data[0]), .Q(REG_E_D_q));  // open: en, clr
  Adder adder_1 (.a(register_1_q), .b(8'h1), .out(adder_1_out));  // open: cin, cout
  assign BUF_E_D_out = rom_1_data[1] ? REG_E_D_q : 8'bz;  // Controlled_Buffer BUF_E_D
  assign BUF_E_D_out = rom_1_data[2] ? rom_1_data_2 : 8'bz;  // Controlled_Buffer BUF_E_E_D
  Register register_1 (.D(adder_1_out), .clk(CLOCK_out), .Q(register_1_q), .clr(RESET_out));  // open: en
  Button CLOCK (.out(CLOCK_out));
  Button RESET (.out(RESET_out));
  Register REG_D (.D(BUF_E_D_out), .clk(rom_1_data[3]), .Q(REG_D_q));  // open: en, clr
  ROM #(.dataWidth(20)) rom_1 (.addr(register_1_q), .data({rom_1_data_2, rom_1_data}));
  assign BUF_E_D_out = rom_1_data[4] ? REG_D_q : 8'bz;  // Controlled_Buffer BUF_R_D
  Register REG_ACU (.D(adder_2_out), .clk(rom_1_data[5]), .Q(REG_ACU_q), .clr(rom_1_data[6]));  // open: en
  Adder adder_2 (.a(REG_ACU_q), .b(BUF_E_D_out), .out(adder_2_out));  // open: cin, cout
  assign BUF_E_D_out = rom_1_data[7] ? REG_ACU_q : 8'bz;  // Controlled_Buffer BUF_ACU
  Register REG_S_D (.D(BUF_E_D_out), .clk(rom_1_data[11]), .Q(SAIDA_DE_DADOS));  // open: en, clr

  // Notes on the sheet:
  //   (0)
  //   BUS DADOS INTERNOS
  //   (1)
  //   (2)
  //   (3)
  //   contents of rom_1 (hex, n*v repeats v):
  //   40 f000 f004 f024 80 880 40
  //   (4)
  //   (5)
  //   (6)
  //   (7)
  //   (11)
endmodule
