// Logisim project Circuitos_Sequencial.circ as structural Verilog: 1 circuit, main circuit main
module main (
  input  S,
  input  R,
  input  D,
  input  E,
  input  J,
  input  K,
  input  S1,
  input  S2
);

  wire and_1_out, and_2_out, and_3_out, ENABLE_out, nand_1_out, nand_2_out, nand_3_out, nand_4_out,
       nand_5_out, nand_6_out, nand_7_out, nand_8_out, nand_9_out, nand_10_out, not_1_out, not_2_out,
       not_3_out, not_4_out, not_5_out, not_6_out, not_7_out, not_8_out, or_1_out, or_2_out, or_3_out,
       START_out;

  not not_1 (not_1_out, S);
  not not_2 (not_2_out, R);
  not not_3 (not_3_out, D);
  not not_4 (not_4_out, E);
  not not_5 (not_5_out, ENABLE_out);
  Button ENABLE (.out(ENABLE_out));
  nand nand_1 (nand_1_out, nand_9_out, K);
  not not_6 (not_6_out, S1);
  not not_7 (not_7_out, S2);
  or or_1 (or_1_out, not_4_out, not_5_out);
  or or_2 (or_2_out, E, not_5_out);
  nand nand_2 (nand_2_out, J, and_1_out);
  nand nand_3 (nand_3_out, not_1_out, nand_4_out);
  LED Q (.in(nand_3_out));
  nand nand_4 (nand_4_out, nand_3_out, not_2_out);
  LED Qc (.in(nand_4_out));
  nand nand_5 (nand_5_out, not_3_out, nand_6_out);
  LED led_1 (.in(nand_5_out));
  nand nand_6 (nand_6_out, nand_5_out, D);
  nand nand_7 (nand_7_out, or_1_out, nand_8_out);
  nand nand_8 (nand_8_out, nand_7_out, or_2_out);
  nand nand_9 (nand_9_out, nand_2_out, and_1_out);
  and and_1 (and_1_out, not_8_out, nand_10_out);
  nand nand_10 (nand_10_out, nand_9_out, nand_1_out);
  and and_2 (and_2_out, not_6_out, not_7_out);
  and and_3 (and_3_out, not_7_out, or_3_out);
  LED led_2 (.in(nand_7_out));
  LED led_3 (.in(nand_9_out));
  not not_8 (not_8_out, START_out);
  Button START (.out(START_out));
  LED led_4 (.in(nand_10_out));
  or or_3 (or_3_out, and_2_out, and_3_out);
  LED led_5 (.in(or_3_out));

  // Notes on the sheet:
  //   REALIMENTAÇÃO
  //   FLIP FLOP RS
  //   FLIP FLOP D
  //   LATCH
  //   FLIP FLOP J K
endmodule
