// Digital circuit LAB_1.1.dig as structural Verilog
module LAB_1_1 (
  input  A0,
  input  A1,
  input  CS,
  input  DE,
  input  A2,
  input  A3
);

  wire and_1_out, diodeforward_1_out, diodeforward_5_out, diodeforward_9_out, diodeforward_13_out,
       driver_1_out, driver_5_out, lab_1_1_o0, lab_1_1_o1, lab_1_1_o2, lab_1_1_o3, lab_1_2_o0, lab_1_2_o1,
       lab_1_2_o2, lab_1_2_o3, switch_1_b, switch_2_b, switch_3_b, switch_4_b, switch_5_b, switch_6_b,
       switch_7_b, switch_8_b, switch_9_b, switch_10_b, switch_11_b, switch_12_b, switch_13_b, switch_14_b,
       switch_15_b, switch_16_b;

  LAB_1 lab_1_1 (.An(A0), .An_plus_1(A1), .CS(CS), .O0(lab_1_1_o0), .O1(lab_1_1_o1), .O2(lab_1_1_o2), .O3(lab_1_1_o3));
  Switch switch_1 (.A(lab_1_1_o0), .B(switch_1_b));
  Switch switch_2 (.A(lab_1_1_o1), .B(switch_2_b));
  Switch switch_3 (.A(lab_1_1_o2), .B(switch_3_b));
  Switch switch_4 (.A(lab_1_1_o3), .B(switch_4_b));
  DiodeForward diodeforward_1 (.in(switch_1_b), .out(diodeforward_1_out));
  DiodeForward diodeforward_2 (.in(switch_2_b), .out(diodeforward_1_out));
  DiodeForward diodeforward_3 (.in(switch_3_b), .out(diodeforward_1_out));
  DiodeForward diodeforward_4 (.in(switch_4_b), .out(diodeforward_1_out));
  PullDown pulldown_1 (.out(diodeforward_1_out));
  LAB_1 lab_1_2 (.An(A2), .An_plus_1(A3), .CS(CS), .O0(lab_1_2_o0), .O1(lab_1_2_o1), .O2(lab_1_2_o2), .O3(lab_1_2_o3));
  Switch switch_5 (.A(lab_1_1_o0), .B(switch_5_b));
  Switch switch_6 (.A(lab_1_1_o1), .B(switch_6_b));
  Switch switch_7 (.A(lab_1_1_o2), .B(switch_7_b));
  Switch switch_8 (.A(lab_1_1_o3), .B(switch_8_b));
  assign driver_1_out = lab_1_2_o0 ? diodeforward_1_out : 1'bz;  // Driver driver_1
  DiodeForward diodeforward_5 (.in(switch_5_b), .out(diodeforward_5_out));
  DiodeForward diodeforward_6 (.in(switch_6_b), .out(diodeforward_5_out));
  DiodeForward diodeforward_7 (.in(switch_7_b), .out(diodeforward_5_out));
  DiodeForward diodeforward_8 (.in(switch_8_b), .out(diodeforward_5_out));
  PullDown pulldown_2 (.out(diodeforward_5_out));
  Switch switch_9 (.A(lab_1_1_o0), .B(switch_9_b));
  Switch switch_10 (.A(lab_1_1_o1), .B(switch_10_b));
  Switch switch_11 (.A(lab_1_1_o2), .B(switch_11_b));
  Switch switch_12 (.A(lab_1_1_o3), .B(switch_12_b));
  assign driver_1_out = lab_1_2_o1 ? diodeforward_5_out : 1'bz;  // Driver driver_2
  DiodeForward diodeforward_9 (.in(switch_9_b), .out(diodeforward_9_out));
  DiodeForward diodeforward_10 (.in(switch_10_b), .out(diodeforward_9_out));
  DiodeForward diodeforward_11 (.in(switch_11_b), .out(diodeforward_9_out));
  DiodeForward diodeforward_12 (.in(switch_12_b), .out(diodeforward_9_out));
  PullDown pulldown_3 (.out(diodeforward_9_out));
  Switch switch_13 (.A(lab_1_1_o0), .B(switch_13_b));
  Switch switch_14 (.A(lab_1_1_o1), .B(switch_14_b));
  Switch switch_15 (.A(lab_1_1_o2), .B(switch_15_b));
  Switch switch_16 (.A(lab_1_1_o3), .B(switch_16_b));
  assign driver_1_out = lab_1_2_o2 ? diodeforward_9_out : 1'bz;  // Driver driver_3
  DiodeForward diodeforward_13 (.in(switch_13_b), .out(diodeforward_13_out));
  DiodeForward diodeforward_14 (.in(switch_14_b), .out(diodeforward_13_out));
  DiodeForward diodeforward_15 (.in(switch_15_b), .out(diodeforward_13_out));
  DiodeForward diodeforward_16 (.in(switch_16_b), .out(diodeforward_13_out));
  PullDown pulldown_4 (.out(diodeforward_13_out));
  assign driver_1_out = lab_1_2_o3 ? diodeforward_13_out : 1'bz;  // Driver driver_4
  and and_1 (and_1_out, CS, DE);
  assign driver_5_out = and_1_out ? driver_1_out : 1'bz;  // Driver driver_5
  LED D0 (.in(driver_5_out));

  // Notes on the sheet:
  //   BUS
  //   ENDEREÇOS
  //   BUS SELEÇÃO
  //   CONTROLE
  //   BUS
  //   ENDEREÇO
  //   BUS
  //   DADOS
endmodule
