// Digital circuit LAB_1.dig as structural Verilog
module LAB_1 (
  input  An,
  input  An_plus_1,
  input  CS,
  output O0,
  output O1,
  output O2,
  output O3
);

  wire not_1_out, not_2_out;

  not not_1 (not_1_out, An);
  not not_2 (not_2_out, An_plus_1);
  and and_1 (O0, not_1_out, CS, not_2_out);
  and and_2 (O1, An, CS, not_2_out);
  and and_3 (O2, not_1_out, CS, An_plus_1);
  and and_4 (O3, An, CS, An_plus_1);
endmodule
