// Logisim project LATCH_AULA4.circ as structural Verilog: 1 circuit, main circuit main
module main (
  input  [3:0] in_1,
  input  [3:0] in_2,
  input  in_3,
  output [3:0] out_4,
  output [3:0] out_5
);

  wire CLOCK_out, CONEXAO1, CONEXAO2, d_ff_1_q, d_ff_1_qn, digital_oscilloscope_1_p5, ENABLE_out, nand_2_out,
       nand_4_out, nand_6_out, nand_8_out, not_2_out, not_3_out, not_4_out, not_5_out, or_1_out, or_2_out,
       or_3_out, or_4_out, or_5_out, or_6_out, or_7_out, or_8_out, RESET_out;

  not not_1 (CONEXAO1, ENABLE_out);
  Button ENABLE (.out(ENABLE_out));
  not not_2 (not_2_out, in_1[0]);
  not not_3 (not_3_out, in_1[1]);
  not not_4 (not_4_out, in_1[2]);
  not not_5 (not_5_out, in_1[3]);
  or or_1 (or_1_out, not_2_out, CONEXAO1);
  or or_2 (or_2_out, in_1[0], CONEXAO1);
  or or_3 (or_3_out, not_4_out, CONEXAO1);
  or or_4 (or_4_out, in_1[2], CONEXAO1);
  or or_5 (or_5_out, not_5_out, CONEXAO1);
  or or_6 (or_6_out, in_1[3], CONEXAO1);
  or or_7 (or_7_out, not_3_out, CONEXAO1);
  or or_8 (or_8_out, in_1[1], CONEXAO1);
  nand nand_1 (out_4[0], or_1_out, nand_2_out);
  nand nand_2 (nand_2_out, out_4[0], or_2_out);
  nand nand_3 (out_4[1], or_7_out, nand_4_out);
  nand nand_4 (nand_4_out, out_4[1], or_8_out);
  nand nand_5 (out_4[2], or_3_out, nand_6_out);
  nand nand_6 (nand_6_out, out_4[2], or_4_out);
  nand nand_7 (out_4[3], or_5_out, nand_8_out);
  nand nand_8 (nand_8_out, out_4[3], or_6_out);
  Hex_Digit_Display hex_digit_display_1 (.value(out_4));  // open: dp
  LED led_1 (.in(out_4[0]));
  LED led_2 (.in(out_4[1]));
  LED led_3 (.in(out_4[2]));
  LED led_4 (.in(out_4[3]));
  Button button_1 (.out(CONEXAO2));
  Register #(.width(4)) register_1 (.D(in_2), .clk(CLOCK_out), .Q(out_5), .clr(RESET_out));  // open: en
  Button CLOCK (.out(CLOCK_out));
  Button RESET (.out(RESET_out));
  Hex_Digit_Display hex_digit_display_2 (.value(out_5));  // open: dp
  D_Flip_Flop d_ff_1 (.D(in_3), .clk(CONEXAO2), .Q(d_ff_1_q), .Qn(d_ff_1_qn));  // open: preset, reset
  LED led_5 (.in(out_5[0]));
  LED led_6 (.in(out_5[1]));
  LED led_7 (.in(out_5[2]));
  LED led_8 (.in(out_5[3]));
  LED led_9 (.in(d_ff_1_q));
  LED led_10 (.in(d_ff_1_qn));
  // Digital_Oscilloscope digital_oscilloscope_1: pin names not known; wires that end beside it: out_5, CONEXAO2, d_ff_1_q, d_ff_1_qn, digital_oscilloscope_1_p5
  Button button_2 (.out(digital_oscilloscope_1_p5));

  // Notes on the sheet:
  //   MANTEM ESTAVEL A SAIDA
  //   CIRCUITO BI ESTAVEL
  //   LATCH 8bits
  //   REGISTRADOR 4 BITS
  //   CIRCUITO BI ESTAVEL
  //   FLIP FLOP D
endmodule
