// Logisim project Revisão.circ as structural Verilog: 8 circuits, main circuit main
module main (
  input  A,
  input  A3,
  input  B,
  input  B3,
  input  A1,
  input  A4,
  input  B1,
  input  B4,
  input  A2,
  input  A5,
  input  in_11,
  input  B5,
  input  in_13
);

  wire b_e_1_s, b_ne_1_s, b_not_1_s, b_nou_1_s, b_ou_1_s, b_xnor_1_s, b_xor_1_s;

  B_OU b_ou_1 (.A(A), .B(B), .S(b_ou_1_s));
  B_E b_e_1 (.A(A1), .B(B1), .S(b_e_1_s));
  B_NOT b_not_1 (.A(A2), .S(b_not_1_s));
  B_XOR b_xor_1 (.A(A5), .B(B5), .S(b_xor_1_s));
  LED S (.in(b_ou_1_s));
  LED S1 (.in(b_e_1_s));
  LED S2 (.in(b_not_1_s));
  LED S5 (.in(b_xor_1_s));
  B_NOU b_nou_1 (.A(A3), .B(B3), .S(b_nou_1_s));
  B_NE b_ne_1 (.A(A4), .B(B4), .S(b_ne_1_s));
  B_XNOR b_xnor_1 (.A(in_11), .B(in_13), .S(b_xnor_1_s));
  LED S3 (.in(b_nou_1_s));
  LED S4 (.in(b_ne_1_s));
  LED led_1 (.in(b_xnor_1_s));

  // Notes on the sheet:
  //   Bloco OU (OR)
  //   Bloco E (AND)
  //   Bloco INVERSOR (NOT)
  //   Bloco EXCLUSIVO (XOR)
  //   Bloco NÃO OU (NOR)
  //   Bloco NÃO E (NAND)
  //   Bloco COINCIDÊNCIA (XNOR)
endmodule

// OU
module B_OU (
  input  A,
  input  B,
  output S
);

  or or_1 (S, B, A);
endmodule

module B_E (
  input  A,
  input  B,
  output S
);

  and and_1 (S, A, B);
endmodule

module B_NOT (
  input  A,
  output S
);

  not not_1 (S, A);
endmodule

module B_NOU (
  input  A,
  input  B,
  output S
);

  wire not_1_out, not_2_out;

  not not_1 (not_1_out, A);
  not not_2 (not_2_out, B);
  and and_1 (S, not_1_out, not_2_out);
endmodule

module B_NE (
  input  A,
  input  B,
  output S
);

  wire not_1_out, not_2_out;

  not not_1 (not_1_out, A);
  not not_2 (not_2_out, B);
  or or_1 (S, not_1_out, not_2_out);
endmodule

module B_XOR (
  input  A,
  input  B,
  output S
);

  wire and_1_out, and_2_out, not_1_out, not_2_out;

  not not_1 (not_1_out, A);
  not not_2 (not_2_out, B);
  and and_1 (and_1_out, not_1_out, B);
  and and_2 (and_2_out, A, not_2_out);
  or or_1 (S, and_1_out, and_2_out);
endmodule

module B_XNOR (
  input  A,
  input  B,
  output S
);

  wire and_1_out, and_2_out, not_1_out, not_2_out;

  not not_1 (not_1_out, A);
  not not_2 (not_2_out, B);
  and and_1 (and_1_out, not_1_out, not_2_out);
  and and_2 (and_2_out, A, B);
  or or_1 (S, and_1_out, and_2_out);
endmodule
