// Logisim project multiplexador.circ as structural Verilog: 3 circuits, main circuit main
module main (
  input  E0,
  input  E1,
  input  E2,
  input  E3
);

  wire C1, cont_1_1_o0, cont_1_1_o1, cont_1_1_o2, cont_1_1_o3, cont_1_2_o0, cont_1_2_o1, cont_1_2_o2,
       cont_1_2_o3, controlled_buffer_1_out, controlled_buffer_5_out, d_ff_1_q, d_ff_2_q, d_ff_3_q, d_ff_4_q;

  Cont_1 cont_1_1 (.CLK(C1), .O0(cont_1_1_o0), .O1(cont_1_1_o1), .O2(cont_1_1_o2), .O3(cont_1_1_o3));  // open: RST
  Clock clock_1 (.out(C1));
  assign controlled_buffer_1_out = cont_1_1_o0 ? E0 : 1'bz;  // Controlled_Buffer controlled_buffer_1
  assign controlled_buffer_1_out = cont_1_1_o1 ? E1 : 1'bz;  // Controlled_Buffer controlled_buffer_2
  assign controlled_buffer_1_out = cont_1_1_o2 ? E2 : 1'bz;  // Controlled_Buffer controlled_buffer_3
  assign controlled_buffer_1_out = cont_1_1_o3 ? E3 : 1'bz;  // Controlled_Buffer controlled_buffer_4
  // Digital_Oscilloscope digital_oscilloscope_1: pin names not known; wires that end beside it: C1, controlled_buffer_1_out
  Cont_1 cont_1_2 (.CLK(C1), .O0(cont_1_2_o0), .O1(cont_1_2_o1), .O2(cont_1_2_o2), .O3(cont_1_2_o3));  // open: RST
  assign controlled_buffer_5_out = cont_1_2_o0 ? controlled_buffer_1_out : 1'bz;  // Controlled_Buffer controlled_buffer_5
  assign controlled_buffer_5_out = cont_1_2_o1 ? controlled_buffer_1_out : 1'bz;  // Controlled_Buffer controlled_buffer_6
  assign controlled_buffer_5_out = cont_1_2_o2 ? controlled_buffer_1_out : 1'bz;  // Controlled_Buffer controlled_buffer_7
  assign controlled_buffer_5_out = cont_1_2_o3 ? controlled_buffer_1_out : 1'bz;  // Controlled_Buffer controlled_buffer_8
  D_Flip_Flop #(.trigger("high")) d_ff_1 (
    .D(controlled_buffer_5_out), .clk(cont_1_2_o0), .Q(d_ff_1_q));  // open: Qn, preset, reset
  D_Flip_Flop #(.trigger("high")) d_ff_2 (
    .D(controlled_buffer_5_out), .clk(cont_1_2_o1), .Q(d_ff_2_q));  // open: Qn, preset, reset
  D_Flip_Flop #(.trigger("high")) d_ff_3 (
    .D(controlled_buffer_5_out), .clk(cont_1_2_o2), .Q(d_ff_3_q));  // open: Qn, preset, reset
  D_Flip_Flop #(.trigger("high")) d_ff_4 (
    .D(controlled_buffer_5_out), .clk(cont_1_2_o3), .Q(d_ff_4_q));  // open: Qn, preset, reset
  LED led_1 (.in(d_ff_1_q));
  LED led_2 (.in(d_ff_2_q));
  LED led_3 (.in(d_ff_3_q));
  LED led_4 (.in(d_ff_4_q));

  // Notes on the sheet:
  //   MULTIPLEXADOR
  //   SINAL MULTIPLEXADO
  //   DEMULTIPLEXADOR
endmodule

module Cont_1 (
  input  CLK,
  input  RST,
  output O0,
  output O1,
  output O2,
  output O3
);

  wire [1:0] adder_1_out, register_1_q;

  Adder #(.width(2)) adder_1 (.a(register_1_q), .b(2'b01), .out(adder_1_out));  // open: cin, cout
  Register #(.width(2)) register_1 (.D(adder_1_out), .clk(CLK), .Q(register_1_q), .clr(RST));  // open: en
  D2X4 d2x4_1 (.A1(register_1_q[1]), .A0(register_1_q[0]), .O0(O0), .O1(O1), .O2(O2), .O3(O3));

  // Notes on the sheet:
  //   CONTADOR 1, 2, 4, 8
endmodule

module D2X4 (
  input  A1,
  input  A0,
  output O0,
  output O1,
  output O2,
  output O3
);

  wire not_1_out, not_2_out;

  not not_1 (not_1_out, A1);
  not not_2 (not_2_out, A0);
  and and_1 (O0, not_1_out, not_2_out);
  and and_2 (O1, not_1_out, A0);
  and and_3 (O2, A1, not_2_out);
  and and_4 (O3, A1, A0);
endmodule
