// Logisim project rom32x2.circ as structural Verilog: 1 circuit, main circuit main
module main (
);

  ROM #(.addrWidth(4), .dataWidth(1)) ROM1 ();  // open: addr, data

  // Notes on the sheet:
  //   BANCO COM [(32X2),CS,DE]
endmodule
